# Fritzing sketch hobd (saved by Fritzing 0.9.3b)
stripboards: 1

parts:
  Part1 = Arduino Nano (Rev3.0)
  Q1 = NPN-Transistor [package="TO92 [THT]"]
  R1 = Resistor [tolerance=±5% resistance=1k package=THT]
  R2 = Resistor [tolerance=±5% resistance=10k package=THT]
  J1_-_A3_10k_NTC_Thermistor = Screw terminal - 2 pins [package=THT]
  J2_-_A1_100psi_Fuel_Pressure = screw terminal, 3 pins
  J3_-_A2_AFR = Screw terminal - 2 pins [package=THT]
  R3 = Resistor [tolerance=±5% resistance=30k package=THT]
  R4 = Resistor [tolerance=±5% resistance=7.5k package=THT]
  J4_-_A0_Volt_Meter_0-25v = Screw terminal - 2 pins [package=THT]
  J5_-_D5_Gnd_Ctrl = Screw terminal - 2 pins [package=THT]
  J6_-_I2C = screw terminal, 4 pins
  J7_-_Power_12v = Screw terminal - 2 pins [package=THT]
  J8_-_D12_DLC = Screw terminal - 2 pins [package=THT]
  Q2 = NPN-Transistor [package="TO92 [THT]"]
  R5 = Resistor [tolerance=±5% resistance=1k package=THT]
  J9_-_D6_Gnd_Ctrl = Screw terminal - 2 pins [package=THT]
  J10_-_D7_Gnd_Ctrl = Screw terminal - 2 pins [package=THT]
  R6 = Resistor [tolerance=±5% resistance=1k package=THT]
  Q3 = NPN-Transistor [package="TO92 [THT]"]
  J11_-_D4_Button = Screw terminal - 2 pins [package=THT]

nets:
  N1: Part1.GND, Q1.E, R2.Pin_1, J2_-_A1_100psi_Fuel_Pressure.pin3, J3_-_A2_AFR.pin2, R4.Pin_1, J4_-_A0_Volt_Meter_0-25v.pin2, J5_-_D5_Gnd_Ctrl.pin2, J6_-_I2C.pin4, J7_-_Power_12v.pin2, J8_-_D12_DLC.pin2, Q2.E, J9_-_D6_Gnd_Ctrl.pin2, J10_-_D7_Gnd_Ctrl.pin2, Q3.E, J11_-_D4_Button.pin2
  N2: Part1.D4, J11_-_D4_Button.pin1
  N3: Part1.D5, R1.Pin_0
  N4: Part1.D6, R5.Pin_0
  N5: Part1.D7, R6.Pin_0
  N6: Part1.D12/MISO, J8_-_D12_DLC.pin1
  N7: Part1.VIN, J7_-_Power_12v.pin1
  N8: Part1.5V, J1_-_A3_10k_NTC_Thermistor.pin1, J2_-_A1_100psi_Fuel_Pressure.pin1, J6_-_I2C.pin3
  N9: Part1.A5, J6_-_I2C.pin1
  N10: Part1.A4, J6_-_I2C.pin2
  N11: Part1.A3, R2.Pin_0, J1_-_A3_10k_NTC_Thermistor.pin2
  N12: Part1.A2, J3_-_A2_AFR.pin1
  N13: Part1.A1, J2_-_A1_100psi_Fuel_Pressure.pin2
  N14: Part1.A0, R3.Pin_1, R4.Pin_0
  N15: Q1.B, R1.Pin_1
  N16: Q1.C, J5_-_D5_Gnd_Ctrl.pin1
  N17: R3.Pin_0, J4_-_A0_Volt_Meter_0-25v.pin1
  N18: Q2.B, Q2.C, R5.Pin_1, J9_-_D6_Gnd_Ctrl.pin1
  N19: J10_-_D7_Gnd_Ctrl.pin1, Q3.C
  N20: R6.Pin_1, Q3.B
